// Logisim project 150140032.circ as structural Verilog
module Homework3 (
  input  a,
  input  b,
  input  c,
  input  d,
  output f
);

  wire nor_1_out, nor_2_out, nor_3_out, nor_4_out, nor_5_out, nor_6_out, nor_7_out;

  nor nor_1 (nor_1_out, a, c);
  nor nor_2 (nor_2_out, b, c);
  nor nor_3 (nor_3_out, a, a);
  nor nor_4 (nor_4_out, nor_1_out, nor_2_out);
  nor nor_5 (nor_5_out, nor_3_out, d);
  nor nor_6 (nor_6_out, nor_4_out, nor_4_out);
  nor nor_7 (nor_7_out, nor_6_out, nor_5_out);
  nor nor_8 (f, nor_7_out, nor_7_out);
endmodule
