// Logisim project 1a.circ as structural Verilog: 1 circuit, main circuit main
module main (
  input  clock,
  input  in_2,
  input  [1:0] FunSel,
  input  Enable,
  input  [7:0] Load__I,
  input  in_6,
  output [7:0] out_7
);

  wire [7:0] adder_1_out, multiplexer_1_out, subtractor_1_out;

  Hex_Digit_Display hex_digit_display_1 (.value(Load__I[7:4]), .dp(in_6));
  Adder adder_1 (.a(out_7), .b(8'h1), .out(adder_1_out));  // open: cin, cout
  Subtractor subtractor_1 (.a(out_7), .b(8'h1), .out(subtractor_1_out));  // open: bin, bout
  Hex_Digit_Display hex_digit_display_2 (.value(Load__I[3:0]), .dp(in_6));
  Multiplexer #(.select(2), .width(8)) multiplexer_1 (
    .in0({8{1'b0}}), .in1(adder_1_out), .in2(subtractor_1_out), .in3(Load__I), .out(multiplexer_1_out),
    .sel(FunSel), .en(Enable));
  D_Flip_Flop d_ff_1 (.clk(clock), .D(multiplexer_1_out[0]), .Q(out_7[0]));  // open: Qn, preset, en, reset
  D_Flip_Flop d_ff_2 (.clk(clock), .D(multiplexer_1_out[1]), .Q(out_7[1]));  // open: Qn, preset, en, reset
  D_Flip_Flop d_ff_3 (.clk(clock), .D(multiplexer_1_out[2]), .Q(out_7[2]));  // open: Qn, preset, en, reset
  D_Flip_Flop d_ff_4 (.clk(clock), .D(multiplexer_1_out[3]), .Q(out_7[3]));  // open: Qn, preset, en, reset
  D_Flip_Flop d_ff_5 (.clk(clock), .D(multiplexer_1_out[4]), .Q(out_7[4]));  // open: Qn, preset, en, reset
  D_Flip_Flop d_ff_6 (.clk(clock), .D(multiplexer_1_out[5]), .Q(out_7[5]));  // open: Qn, preset, en, reset
  D_Flip_Flop d_ff_7 (.clk(clock), .D(multiplexer_1_out[6]), .Q(out_7[6]));  // open: Qn, preset, en, reset
  D_Flip_Flop d_ff_8 (.clk(clock), .D(multiplexer_1_out[7]), .Q(out_7[7]));  // open: Qn, preset, en, reset
  Hex_Digit_Display hex_digit_display_3 (.value(out_7[7:4]), .dp(in_2));
  Hex_Digit_Display hex_digit_display_4 (.value(out_7[3:0]), .dp(in_2));
endmodule
