// Logisim project 2b.circ as structural Verilog: 1 circuit, main circuit main
module main (
  input  clock,
  input  [7:0] Load,
  input  [1:0] FunSel,
  input  in_4,
  input  in_5,
  input  [1:0] OutCSel,
  input  [2:0] RegSel,
  output [7:0] OutA
);

  wire [7:0] AR_out_7, PC_out_7, SP_out_7;

  Hex_Digit_Display hex_digit_display_1 (.value(Load[7:4]), .dp(in_4));
  Hex_Digit_Display hex_digit_display_2 (.value(Load[3:0]), .dp(in_4));
  _1a_main PC (
    .clock(clock), .FunSel(FunSel), .Enable(RegSel[2]), .Load__I(Load), .out_7(PC_out_7));  // open: in_2, in_6
  _1a_main AR (
    .clock(clock), .FunSel(FunSel), .Enable(RegSel[1]), .Load__I(Load), .out_7(AR_out_7));  // open: in_2, in_6
  _1a_main SP (
    .clock(clock), .FunSel(FunSel), .Enable(RegSel[0]), .Load__I(Load), .out_7(SP_out_7));  // open: in_2, in_6
  Multiplexer #(.select(2), .width(8), .enable("false")) multiplexer_1 (
    .in0(PC_out_7), .in1(PC_out_7), .in2(AR_out_7), .in3(SP_out_7), .out(OutA), .sel(OutCSel));
  Hex_Digit_Display hex_digit_display_3 (.value(OutA[7:4]), .dp(in_5));
  Hex_Digit_Display hex_digit_display_4 (.value(OutA[3:0]), .dp(in_5));

  // Notes on the sheet:
  //   input
  //   output
endmodule
