// Logisim project Project2Part2.circ as structural Verilog: 1 circuit, main circuit main
module main (
  input  [1:0] FunSel1,
  input  [3:0] FunSel2,
  input  clock,
  input  [3:0] RegSel1,
  input  [1:0] OutASel,
  input  [1:0] OutBSel,
  input  [1:0] FunSel3,
  input  [1:0] MuxASel,
  input  [2:0] RegSel3,
  input  [1:0] MuxBSel,
  input  L_S,
  input  [1:0] OutCSel,
  input  [1:0] FunSel4,
  input  L_H,
  output [7:0] IR_8_15,
  output [7:0] IR_0_7
);

  wire en, not_1_out;
  wire [3:0] ALU_out_6;
  wire [7:0] ALU_output, main_1_outa, main_1_outb, main_3_outa, multiplexer_1_out, multiplexer_2_out,
       ram_1_data;

  Hex_Digit_Display hex_digit_display_1 (.value(IR_8_15[7:4]));  // open: dp
  Hex_Digit_Display hex_digit_display_2 (.value(IR_8_15[3:0]));  // open: dp
  _2a_main main_1 (
    .clock(clock), .Load(multiplexer_1_out), .FunSel(FunSel1), .RegSel(RegSel1), .OutASel(OutASel),
    .OutBSel(OutBSel), .OutA(main_1_outa), .OutB(main_1_outb));  // open: in_4, in_5, in_7
  Multiplexer #(.select(2), .width(8)) multiplexer_1 (
    .in0(ALU_output), .in1(main_3_outa), .in2(ram_1_data), .in3(IR_0_7), .out(multiplexer_1_out),
    .sel(MuxASel), .en(en));
  _2c_main main_2 (
    .Enable(en), .clock(clock), .\input (ram_1_data), .Output({IR_8_15, IR_0_7}), .L_H(L_H), .Funsel(FunSel4));  // open: in_4
  Project2Part1_main ALU (
    .FunSel(FunSel2), .cin(ALU_out_6[2]), .A(main_1_outa), .B(main_1_outb), .Output(ALU_output),
    .out_6(ALU_out_6));
  Multiplexer #(.select(2), .width(8)) multiplexer_2 (
    .in0(ALU_output), .in1(main_3_outa), .in2(ram_1_data), .in3(IR_0_7), .out(multiplexer_2_out),
    .sel(MuxBSel), .en(en));
  _2b_main main_3 (
    .clock(clock), .Load(multiplexer_2_out), .FunSel(FunSel3), .RegSel(RegSel3), .OutCSel(OutCSel),
    .OutA(main_3_outa));  // open: in_4, in_5
  not not_1 (not_1_out, L_S);
  RAM #(.bus("separate")) ram_1 (
    .addr(main_3_outa), .din(ALU_output), .data(ram_1_data), .str(not_1_out), .clk(clock), .ld(L_S));  // open: sel, clr

  // Other names for the same wires on the sheet: cl = clock
endmodule
