// Logisim project Project3.circ as structural Verilog: 1 circuit, main circuit main
module main (
  input  [4:0] in_1,
  input  in_2,
  input  in_3,
  input  in_4
);

  wire AM, and_1_out, and_2_out, and_3_out, and_4_out, and_5_out, and_6_out, and_7_out, and_8_out, and_9_out,
       and_10_out, and_11_out, and_12_out, and_13_out, and_14_out, and_15_out, and_16_out, and_17_out,
       and_18_out, and_19_out, and_20_out, and_21_out, and_22_out, and_23_out, and_24_out, and_25_out,
       and_26_out, and_27_out, and_28_out, and_29_out, and_30_out, and_31_out, and_32_out, and_33_out,
       and_34_out, and_35_out, and_36_out, and_37_out, and_38_out, and_39_out, and_40_out, and_41_out,
       and_42_out, and_43_out, and_44_out, and_45_out, and_46_out, and_47_out, and_48_out, and_49_out,
       and_50_out, and_51_out, and_52_out, and_53_out, and_54_out, and_55_out, and_56_out, and_57_out,
       and_58_out, and_59_out, and_60_out, and_61_out, and_62_out, and_63_out, and_64_out, and_65_out,
       and_66_out, and_67_out, and_68_out, and_69_out, and_70_out, and_71_out, and_72_out, and_73_out,
       and_74_out, and_75_out, and_76_out, and_77_out, and_78_out, and_79_out, and_80_out, and_81_out,
       and_82_out, and_83_out, and_84_out, and_85_out, and_86_out, and_87_out, and_89_out, and_90_out,
       and_91_out, and_92_out, and_93_out, and_94_out, and_95_out, and_96_out, and_97_out, and_98_out,
       and_99_out, and_100_out, and_101_out, and_102_out, and_103_out, and_104_out, and_105_out, and_106_out,
       and_107_out, and_108_out, and_109_out, and_110_out, and_111_out, and_112_out, and_113_out,
       and_114_out, and_115_out, and_116_out, and_117_out, and_118_out, and_119_out, and_120_out,
       and_121_out, and_122_out, and_123_out, and_124_out, and_125_out, and_126_out, and_127_out,
       and_128_out, and_129_out, and_130_out, and_131_out, and_132_out, and_133_out, and_134_out,
       and_137_out, and_138_out, and_139_out, and_140_out, and_141_out, and_142_out, and_143_out,
       and_144_out, CLEAR, D0, D1, D2, D3, D4, D5, D6, D7, D8, D9, D10, D11, D12, D13, D14, D15, D16, D17,
       D18, D23, D24, D5910, D56910, decoder_7_out0, decoder_7_out1, decoder_8_out0, decoder_8_out1, DR_F1,
       IR_E, L_H, L_S, nand_1_out, not_1_out, or_1_out, or_2_out, or_3_out, or_4_out, or_5_out, or_6_out,
       or_7_out, or_8_out, or_9_out, or_10_out, or_12_out, or_13_out, or_14_out, or_15_out, or_16_out,
       or_17_out, or_18_out, or_19_out, or_20_out, or_21_out, or_22_out, or_23_out, or_24_out, or_25_out,
       or_26_out, or_27_out, or_28_out, or_29_out, or_30_out, or_31_out, or_32_out, or_33_out, or_34_out,
       or_35_out, or_36_out, or_38_out, or_39_out, or_40_out, or_41_out, or_44_out, or_45_out, or_46_out,
       or_47_out, or_48_out, or_49_out, or_50_out, or_51_out, or_53_out, or_54_out, or_55_out, or_56_out,
       or_57_out, or_59_out, or_60_out, or_61_out, or_62_out, or_63_out, T0, T1, T2, T3, T4, T5, T6, T7, T8,
       T9, T10, T11, T12, T13, T14, T15, xor_1_out, xor_2_out, xor_3_out, xor_4_out, xor_5_out, xor_6_out,
       xor_7_out, xor_8_out, xor_9_out, xor_10_out;
  wire [1:0] FS1, FS3, FS4, MAS, MBS, OAS, OBS, OCS;
  wire [1:1] DR_L2;
  wire [2:0] Decoded_3bit_DR, Decoded_3bit_SR1, RS3;
  wire [3:0] counter_1_q, Decoded_4bit_DR, Decoded_4bit_RS, Decoded_4bit_SR1, Decoded_4bit_SR2, FS2, RS1;
  wire [7:0] IR_0_7;
  wire [7:3] IR_8_15;

  and and_1 (and_1_out, T2, D0);
  and and_2 (and_2_out, T2, AM, D1);
  and and_3 (and_3_out, T2, ~AM, D14);  // AND_Gate
  or or_1 (or_1_out, T4, T3);
  and and_4 (and_4_out, or_1_out, ~AM, D14);  // AND_Gate
  and and_5 (and_5_out, T2, D18);
  and and_6 (and_6_out, T3, ~AM, D0);  // AND_Gate
  and and_7 (and_7_out, T2, D23, DR_F1, ~IR_0_7[7]);  // AND_Gate
  xor xor_1 (xor_1_out, IR_0_7[7], IR_0_7[4]);
  and and_8 (and_8_out, T2, D23, DR_F1, IR_0_7[7]);
  assign MBS = and_8_out ? 2'b01 : 2'bz;  // Controlled_Buffer controlled_buffer_1
  xor xor_2 (xor_2_out, IR_0_7[7], IR_0_7[4]);
  and and_9 (and_9_out, T2, D3);
  and and_10 (and_10_out, D7, T3, IR_0_7[7]);
  or or_2 (or_2_out, D7, D8);
  or or_3 (or_3_out, and_7_out, and_11_out, and_12_out, and_13_out);
  assign MBS = or_3_out ? 2'b00 : 2'bz;  // Controlled_Buffer controlled_buffer_2
  and and_11 (and_11_out, T3, D56910, DR_F1, xor_1_out);
  and and_12 (and_12_out, T2, D56910, DR_F1, ~IR_0_7[7], ~IR_0_7[4]);  // AND_Gate
  and and_13 (and_13_out, T4, D56910, DR_F1, IR_0_7[7], IR_0_7[4]);
  and and_14 (and_14_out, D8, T3, IR_0_7[7]);
  and and_15 (and_15_out, T2, D4);
  or or_4 (or_4_out, T0, T1);
  and and_16 (and_16_out, T3, D18);
  and and_17 (and_17_out, T2, D18);
  and and_18 (and_18_out, T4, D56910, DR_F1, IR_0_7[7], IR_0_7[4]);
  and and_19 (and_19_out, T3, D56910, DR_F1, xor_2_out);
  and and_20 (and_20_out, T2, D0);
  and and_21 (and_21_out, T3, ~AM, D0);  // AND_Gate
  and and_22 (and_22_out, T2, AM, D1);
  or or_5 (or_5_out, T3, T2, T4);
  and and_23 (and_23_out, or_5_out, ~AM, D14);  // AND_Gate
  and and_24 (and_24_out, T2, D23, DR_F1);
  and and_25 (and_25_out, T2, D56910, DR_F1, ~IR_0_7[7], ~IR_0_7[4]);  // AND_Gate
  or or_6 (or_6_out, and_9_out, and_10_out);
  or or_7 (or_7_out, T3, T4);
  and and_26 (and_26_out, or_7_out, ~AM, D14);  // AND_Gate
  assign L_H = T0 ? 1'b0 : 1'bz;  // Controlled_Buffer controlled_buffer_3
  assign L_H = T1 ? 1'b1 : 1'bz;  // Controlled_Buffer controlled_buffer_4
  xor xor_3 (xor_3_out, IR_0_7[7], IR_0_7[4]);
  and and_27 (and_27_out, T2, D5910, IR_0_7[7], IR_0_7[4]);
  and and_28 (and_28_out, or_2_out, T3, ~IR_0_7[7]);  // AND_Gate
  Project2Part2_main main_1 (
    .FunSel1(FS1), .FunSel2(FS2), .clock(in_2), .RegSel1(RS1), .OutASel(OAS), .OutBSel(OBS), .MuxASel(MAS),
    .RegSel3(RS3), .MuxBSel(MBS), .L_S(L_S), .OutCSel(OCS), .FunSel3(FS3), .FunSel4(FS4), .L_H(L_H),
    .MAS_E(in_3), .MBS_E(in_4), .IR_E(IR_E), .IR_8_15({IR_8_15, DR_F1, DR_L2[1], AM}), .IR_0_7(IR_0_7));
  or or_8 (or_8_out, and_1_out, and_2_out, and_3_out);
  assign MBS = or_8_out ? 2'b11 : 2'bz;  // Controlled_Buffer controlled_buffer_5
  or or_9 (or_9_out, and_4_out, and_5_out, and_6_out);
  assign MBS = or_9_out ? 2'b10 : 2'bz;  // Controlled_Buffer controlled_buffer_6
  assign FS3 = or_6_out ? 2'b10 : 2'bz;  // Controlled_Buffer controlled_buffer_7
  and and_29 (and_29_out, T3, AM, D1);
  and and_30 (and_30_out, T2, D3);
  and and_31 (and_31_out, T2, D18);
  and and_32 (and_32_out, T3, D0);
  and and_33 (and_33_out, T4, ~AM, D0);  // AND_Gate
  and and_34 (and_34_out, T2, AM, D1);
  or or_10 (or_10_out, T0, T1);
  assign FS4 = T0 ? 2'b11 : 2'bz;  // Controlled_Buffer controlled_buffer_8
  assign FS4 = T1 ? 2'b11 : 2'bz;  // Controlled_Buffer controlled_buffer_9
  or or_11 (IR_E, T0, T1);
  and and_35 (and_35_out, T2, D4);
  and and_36 (and_36_out, T4, ~AM, D0);  // AND_Gate
  and and_37 (and_37_out, D23, T2, ~DR_F1);  // AND_Gate
  and and_38 (and_38_out, T2, D56910, ~DR_F1, ~IR_0_7[7], ~IR_0_7[4]);  // AND_Gate
  and and_39 (and_39_out, T3, D56910, ~DR_F1, xor_3_out);  // AND_Gate
  and and_40 (and_40_out, T4, D56910, ~DR_F1, IR_0_7[7], IR_0_7[4]);  // AND_Gate
  or or_12 (or_12_out, and_27_out, and_28_out);
  and and_41 (and_41_out, T2, D6, IR_0_7[7], IR_0_7[4]);
  buf or_13 (or_13_out, and_41_out);  // OR_Gate
  and and_42 (and_42_out, T2, D5910, ~IR_0_7[7], IR_0_7[4]);  // AND_Gate
  or or_14 (or_14_out, and_42_out, and_43_out, and_44_out);
  and and_43 (and_43_out, T3, D5910, IR_0_7[7], IR_0_7[4]);
  and and_44 (and_44_out, T2, D6, IR_0_7[7], ~IR_0_7[4]);  // AND_Gate
  and and_45 (and_45_out, T2, D5910, IR_0_7[7], ~IR_0_7[4]);  // AND_Gate
  or or_15 (or_15_out, and_45_out, and_46_out, and_47_out);
  and and_46 (and_46_out, T2, D6, ~IR_0_7[7], IR_0_7[4]);  // AND_Gate
  and and_47 (and_47_out, T3, D6, IR_0_7[7], IR_0_7[4]);
  or or_16 (or_16_out, and_14_out, and_15_out, or_4_out, and_16_out);
  assign FS3 = or_16_out ? 2'b01 : 2'bz;  // Controlled_Buffer controlled_buffer_10
  or or_17 (or_17_out, and_17_out, and_18_out, and_19_out, and_20_out, and_21_out, and_22_out, and_23_out, and_24_out, and_25_out);
  assign FS3 = or_17_out ? 2'b11 : 2'bz;  // Controlled_Buffer controlled_buffer_11
  or or_18 (or_18_out, and_29_out, and_30_out);
  assign L_S = or_18_out ? 1'b0 : 1'bz;  // Controlled_Buffer controlled_buffer_12
  or or_19 (or_19_out, and_31_out, and_32_out, and_33_out, and_34_out, or_10_out, and_26_out);
  assign L_S = or_19_out ? 1'b1 : 1'bz;  // Controlled_Buffer controlled_buffer_13
  or or_20 (or_20_out, and_35_out, and_36_out);
  or or_21 (or_21_out, and_37_out, and_38_out, and_39_out, and_40_out);
  assign RS1 = or_21_out ? Decoded_4bit_DR : 4'bz;  // Controlled_Buffer controlled_buffer_14
  assign RS1 = or_12_out ? Decoded_4bit_SR1 : 4'bz;  // Controlled_Buffer controlled_buffer_15
  assign RS1 = or_13_out ? Decoded_4bit_SR2 : 4'bz;  // Controlled_Buffer controlled_buffer_16
  assign RS1 = or_14_out ? ~Decoded_4bit_SR1 : 4'bz;  // Controlled_Inverter controlled_inverter_1
  assign RS1 = or_15_out ? ~Decoded_4bit_SR2 : 4'bz;  // Controlled_Inverter controlled_inverter_2
  or or_22 (or_22_out, D7, D8);
  assign RS1 = or_20_out ? Decoded_4bit_RS : 4'bz;  // Controlled_Buffer controlled_buffer_17
  Decoder #(.select(5), .enable("false")) decoder_1 (
    .out0(D0), .out1(D1), .out2(D2), .out3(D3), .out4(D4), .out5(D5), .out6(D6), .out7(D7), .out8(D8),
    .out9(D9), .out10(D10), .out11(D11), .out12(D12), .out13(D13), .out14(D14), .out15(D15), .out16(D16),
    .out17(D17), .out18(D18), .sel(IR_8_15));  // open: out19, out20, out21, out22, out23, out24, out25, out26, out27, out28, out29, out30, out31
  and and_48 (and_48_out, T2, D0);
  and and_49 (and_49_out, T3, ~AM, D0);  // AND_Gate
  and and_50 (and_50_out, T2, AM, D1);
  and and_51 (and_51_out, D14, ~AM, or_23_out);  // AND_Gate
  or or_23 (or_23_out, T3, T2);
  or or_24 (or_24_out, T0, T1);
  and and_52 (and_52_out, T4, ~AM, D14);  // AND_Gate
  and and_53 (and_53_out, T2, D18);
  and and_54 (and_54_out, T2, D23, DR_F1, ~IR_0_7[7]);  // AND_Gate
  and and_55 (and_55_out, T2, D23, DR_F1, IR_0_7[7]);
  and and_56 (and_56_out, T2, D56910, DR_F1, ~IR_0_7[7], ~IR_0_7[4]);  // AND_Gate
  and and_57 (and_57_out, T3, D56910, DR_F1, xor_4_out);
  xor xor_4 (xor_4_out, IR_0_7[7], IR_0_7[4]);
  and and_58 (and_58_out, T4, D56910, DR_F1, IR_0_7[7], IR_0_7[4]);
  and and_59 (and_59_out, or_22_out, T3, IR_0_7[7]);
  or or_25 (or_25_out, T4, T3);
  and and_60 (and_60_out, T2, D3);
  and and_61 (and_61_out, T2, D4);
  and and_62 (and_62_out, T3, D18);
  or or_26 (or_26_out, and_48_out, and_49_out, and_50_out, and_51_out);
  or or_27 (or_27_out, and_54_out, and_55_out, and_56_out, and_57_out, and_58_out);
  buf or_28 (or_28_out, and_59_out);  // OR_Gate
  and and_63 (and_63_out, T2, D56910, ~IR_0_7[7], IR_0_7[4]);  // AND_Gate
  and and_64 (and_64_out, T3, D56910, IR_0_7[7], IR_0_7[4]);
  and and_65 (and_65_out, T2, D23, IR_0_7[7]);
  and and_66 (and_66_out, T2, D56910, IR_0_7[7], ~IR_0_7[4]);  // AND_Gate
  and and_67 (and_67_out, T2, D56910, IR_0_7[7], IR_0_7[4]);
  and and_68 (and_68_out, T3, D0);
  and and_69 (and_69_out, T4, ~AM, D0);  // AND_Gate
  and and_70 (and_70_out, T3, AM, D1);
  and and_71 (and_71_out, or_25_out, ~AM, D14);  // AND_Gate
  and and_72 (and_72_out, T2, D4);
  and and_73 (and_73_out, T2, D18);
  and and_74 (and_74_out, T2, D3);
  Counter #(.width(4), .max('hf)) counter_1 (.Q(counter_1_q), .clk(in_2), .clr(CLEAR));  // open: load, D, count, carry
  Decoder #(.select(4), .enable("false")) decoder_2 (
    .out0(T0), .out1(T1), .out2(T2), .out3(T3), .out4(T4), .out5(T5), .out6(T6), .out7(T7), .out8(T8),
    .out9(T9), .out10(T10), .out11(T11), .out12(T12), .out13(T13), .out14(T14), .out15(T15), .sel(counter_1_q));
  or or_29 (or_29_out, and_60_out, and_61_out, and_62_out);
  assign RS3 = or_29_out ? 3'b001 : 3'bz;  // Controlled_Buffer controlled_buffer_18
  assign RS3 = or_26_out ? 3'b010 : 3'bz;  // Controlled_Buffer controlled_buffer_19
  or or_30 (or_30_out, or_24_out, and_52_out, and_53_out);
  assign RS3 = or_30_out ? 3'b100 : 3'bz;  // Controlled_Buffer controlled_buffer_20
  assign RS3 = or_27_out ? Decoded_3bit_DR : 3'bz;  // Controlled_Buffer controlled_buffer_21
  assign RS3 = or_28_out ? Decoded_3bit_SR1 : 3'bz;  // Controlled_Buffer controlled_buffer_22
  or or_31 (or_31_out, and_63_out, and_64_out);
  assign OCS = or_31_out ? IR_0_7[3:2] : 2'bz;  // Controlled_Buffer controlled_buffer_23
  or or_32 (or_32_out, and_65_out, and_66_out, and_67_out);
  or or_33 (or_33_out, and_68_out, and_69_out, and_70_out, and_71_out);
  assign OCS = or_33_out ? 2'b10 : 2'bz;  // Controlled_Buffer controlled_buffer_24
  or or_34 (or_34_out, and_72_out, and_73_out, and_74_out);
  assign OCS = or_34_out ? 2'b11 : 2'bz;  // Controlled_Buffer controlled_buffer_25
  or or_35 (or_35_out, T0, T1);
  xor xor_5 (xor_5_out, IR_0_7[7], IR_0_7[4]);
  or or_36 (or_36_out, IR_0_7[7], IR_0_7[4]);
  assign OCS = or_32_out ? IR_0_7[6:5] : 2'bz;  // Controlled_Buffer controlled_buffer_26
  assign OCS = or_35_out ? 2'b00 : 2'bz;  // Controlled_Buffer controlled_buffer_27
  and and_75 (and_75_out, T2, D56910, ~DR_F1, ~IR_0_7[7], ~IR_0_7[4]);  // AND_Gate
  and and_76 (and_76_out, T4, D56910, ~DR_F1, IR_0_7[7], IR_0_7[4]);  // AND_Gate
  and and_77 (and_77_out, T3, D56910, ~DR_F1, xor_5_out);  // AND_Gate
  and and_78 (and_78_out, T2, D23, ~DR_F1, ~IR_0_7[7]);  // AND_Gate
  and and_79 (and_79_out, T2, D23, ~DR_F1, IR_0_7[7]);  // AND_Gate
  and and_80 (and_80_out, T2, D56910, or_36_out);
  and and_81 (and_81_out, T3, D56910, IR_0_7[7], IR_0_7[4]);
  and and_82 (and_82_out, T3, AM, D0);
  and and_83 (and_83_out, T4, ~AM, D0);  // AND_Gate
  and and_84 (and_84_out, T2, D4);
  and and_85 (and_85_out, T2, D11, ~IR_0_7[7]);  // AND_Gate
  or or_37 (D23, D2, D8, D7);
  or or_38 (or_38_out, and_75_out, and_76_out, and_77_out, and_78_out);
  or or_39 (or_39_out, and_82_out, and_83_out, and_84_out);
  assign MAS = or_39_out ? 2'b10 : 2'bz;  // Controlled_Buffer controlled_buffer_28
  buf or_40 (or_40_out, and_85_out);  // OR_Gate
  assign MAS = or_40_out ? IR_0_7[6:5] : 2'bz;  // Controlled_Buffer controlled_buffer_29
  assign MAS = or_38_out ? 2'b00 : 2'bz;  // Controlled_Buffer controlled_buffer_30
  or or_41 (or_41_out, and_79_out, and_80_out, and_81_out);
  assign MAS = or_41_out ? 2'b01 : 2'bz;  // Controlled_Buffer controlled_buffer_31
  and and_86 (and_86_out, T3, D0);
  and and_87 (and_87_out, T4, ~AM, D0);  // AND_Gate
  or or_42 (D56910, D5, D6, D9, D10);
  or or_43 (D5910, D5, D9, D10);
  and and_88 (D24, nand_1_out, or_45_out);
  Decoder #(.select(2)) decoder_3 (
    .out0(Decoded_4bit_RS[0]), .out1(Decoded_4bit_RS[1]), .out2(Decoded_4bit_RS[2]),
    .out3(Decoded_4bit_RS[3]), .sel({DR_F1, DR_L2[1]}), .en(or_44_out));
  or or_44 (or_44_out, and_86_out, and_87_out);
  nand nand_1 (nand_1_out, IR_0_7[7], DR_F1);
  or or_45 (or_45_out, D11, D12, D13);
  or or_46 (or_46_out, IR_0_7[7], IR_0_7[4]);
  and and_89 (and_89_out, T2, D3);
  and and_90 (and_90_out, T2, AM, D1);
  and and_91 (and_91_out, T4, D56910, ~DR_F1, IR_0_7[7], IR_0_7[4]);  // AND_Gate
  xor xor_6 (xor_6_out, IR_0_7[7], IR_0_7[4]);
  and and_92 (and_92_out, T3, D0);
  and and_93 (and_93_out, T4, ~AM, D0);  // AND_Gate
  and and_94 (and_94_out, D23, T2, ~DR_F1);  // AND_Gate
  and and_95 (and_95_out, T2, D4);
  and and_96 (and_96_out, T2, D56910, ~DR_F1, ~IR_0_7[7], ~IR_0_7[4]);  // AND_Gate
  and and_97 (and_97_out, T2, D56910, or_46_out);
  and and_98 (and_98_out, T3, D56910, IR_0_7[7], IR_0_7[4]);
  and and_99 (and_99_out, D7, T3, ~IR_0_7[7]);  // AND_Gate
  and and_100 (and_100_out, D8, T3, ~IR_0_7[7]);  // AND_Gate
  xor xor_7 (xor_7_out, IR_0_7[7], IR_0_7[4]);
  xor xor_8 (xor_8_out, IR_0_7[7], IR_0_7[4]);
  xor xor_9 (xor_9_out, IR_0_7[7], IR_0_7[4]);
  xor xor_10 (xor_10_out, IR_0_7[7], IR_0_7[4]);
  and and_101 (and_101_out, T3, D5910, IR_0_7[7], ~IR_0_7[4]);  // AND_Gate
  and and_102 (and_102_out, T2, D6, ~IR_0_7[7], ~IR_0_7[4]);  // AND_Gate
  and and_103 (and_103_out, T3, D6, ~IR_0_7[7], IR_0_7[4]);  // AND_Gate
  and and_104 (and_104_out, T4, D6, IR_0_7[7], IR_0_7[4]);
  and and_105 (and_105_out, T2, D5910, ~IR_0_7[7], ~IR_0_7[4]);  // AND_Gate
  and and_106 (and_106_out, T2, D6, ~IR_0_7[7], ~IR_0_7[4]);  // AND_Gate
  and and_107 (and_107_out, T3, D56910, ~DR_F1, xor_6_out);  // AND_Gate
  and and_108 (and_108_out, T2, D23, ~IR_0_7[7]);  // AND_Gate
  and and_109 (and_109_out, T2, D5, ~IR_0_7[7], ~IR_0_7[4]);  // AND_Gate
  and and_110 (and_110_out, T3, D5, xor_7_out);
  and and_111 (and_111_out, T4, D5, IR_0_7[7], IR_0_7[4]);
  and and_112 (and_112_out, T2, D6, ~IR_0_7[7], ~IR_0_7[4]);  // AND_Gate
  and and_113 (and_113_out, T3, D6, xor_8_out);
  and and_114 (and_114_out, T4, D6, IR_0_7[7], IR_0_7[4]);
  and and_115 (and_115_out, T2, D9, ~IR_0_7[7], ~IR_0_7[4]);  // AND_Gate
  and and_116 (and_116_out, T3, D9, xor_9_out);
  and and_117 (and_117_out, T4, D9, IR_0_7[7], IR_0_7[4]);
  and and_118 (and_118_out, T2, D10, ~IR_0_7[7], ~IR_0_7[4]);  // AND_Gate
  and and_119 (and_119_out, T3, D10, xor_10_out);
  and and_120 (and_120_out, T4, D10, IR_0_7[7], IR_0_7[4]);
  and and_121 (and_121_out, T3, D5910, ~IR_0_7[7], IR_0_7[4]);  // AND_Gate
  and and_122 (and_122_out, T2, D5910, ~IR_0_7[7], ~IR_0_7[4]);  // AND_Gate
  and and_123 (and_123_out, T2, D23, ~DR_F1, ~IR_0_7[7]);  // AND_Gate
  and and_124 (and_124_out, T2, D23, DR_F1, ~IR_0_7[7]);  // AND_Gate
  and and_125 (and_125_out, T4, D5910, IR_0_7[7], IR_0_7[4]);
  and and_126 (and_126_out, T3, D6, IR_0_7[7], ~IR_0_7[4]);  // AND_Gate
  or or_47 (or_47_out, and_101_out, and_102_out, and_103_out, and_104_out);
  assign OAS = or_47_out ? IR_0_7[3:2] : 2'bz;  // Controlled_Buffer controlled_buffer_32
  or or_48 (or_48_out, and_89_out, and_90_out);
  assign OAS = or_48_out ? {DR_F1, DR_L2[1]} : 2'bz;  // Controlled_Buffer controlled_buffer_33
  buf or_49 (or_49_out, and_106_out);  // OR_Gate
  and and_127 (and_127_out, T3, D5910, ~IR_0_7[7], IR_0_7[4]);  // AND_Gate
  or or_50 (or_50_out, and_127_out, and_128_out, and_129_out);
  and and_128 (and_128_out, T4, D5910, IR_0_7[7], IR_0_7[4]);
  and and_129 (and_129_out, T3, D6, IR_0_7[7], ~IR_0_7[4]);  // AND_Gate
  and and_130 (and_130_out, T3, D5910, IR_0_7[7], ~IR_0_7[4]);  // AND_Gate
  or or_51 (or_51_out, and_130_out, and_131_out, and_132_out);
  and and_131 (and_131_out, T3, D6, ~IR_0_7[7], IR_0_7[4]);  // AND_Gate
  and and_132 (and_132_out, T4, D6, IR_0_7[7], IR_0_7[4]);
  Decoder #(.select(2), .enable("false")) decoder_4 (
    .out0(Decoded_4bit_DR[3]), .out1(Decoded_4bit_DR[2]), .out2(Decoded_4bit_DR[1]),
    .out3(Decoded_4bit_DR[0]), .sel({DR_L2[1], AM}));
  Decoder #(.select(2), .enable("false")) decoder_5 (
    .out0(Decoded_4bit_SR1[3]), .out1(Decoded_4bit_SR1[2]), .out2(Decoded_4bit_SR1[1]),
    .out3(Decoded_4bit_SR1[0]), .sel(IR_0_7[6:5]));
  Decoder #(.select(2), .enable("false")) decoder_6 (
    .out0(Decoded_4bit_SR2[3]), .out1(Decoded_4bit_SR2[2]), .out2(Decoded_4bit_SR2[1]),
    .out3(Decoded_4bit_SR2[0]), .sel(IR_0_7[3:2]));
  or or_52 (Decoded_3bit_DR[2], decoder_7_out0, decoder_7_out1);
  Decoder #(.select(2), .enable("false")) decoder_7 (
    .out0(decoder_7_out0), .out1(decoder_7_out1), .out2(Decoded_3bit_DR[1]), .out3(Decoded_3bit_DR[0]),
    .sel({DR_L2[1], AM}));
  Decoder #(.select(2), .enable("false")) decoder_8 (
    .out0(decoder_8_out0), .out1(decoder_8_out1), .out2(Decoded_3bit_SR1[1]), .out3(Decoded_3bit_SR1[0]),
    .sel(IR_0_7[6:5]));
  or or_53 (or_53_out, and_91_out, and_107_out, and_92_out, and_93_out, and_94_out, and_95_out, and_96_out, and_97_out, and_98_out);
  assign FS1 = or_53_out ? 2'b11 : 2'bz;  // Controlled_Buffer controlled_buffer_34
  or or_54 (or_54_out, and_99_out, and_99_out);
  assign FS1 = or_54_out ? 2'b10 : 2'bz;  // Controlled_Buffer controlled_buffer_35
  or or_55 (or_55_out, and_100_out, and_100_out);
  assign FS1 = or_55_out ? 2'b01 : 2'bz;  // Controlled_Buffer controlled_buffer_36
  and and_133 (and_133_out, T2, AM, D1);
  and and_134 (and_134_out, T2, D3);
  or or_56 (or_56_out, and_121_out, and_122_out, and_123_out, and_124_out, and_125_out, and_126_out);
  buf or_57 (or_57_out, and_105_out);  // OR_Gate
  assign OBS = or_57_out ? IR_0_7[3:2] : 2'bz;  // Controlled_Buffer controlled_buffer_37
  assign OBS = or_49_out ? IR_0_7[6:5] : 2'bz;  // Controlled_Buffer controlled_buffer_38
  assign OBS = or_50_out ? ~IR_0_7[6:5] : 2'bz;  // Controlled_Inverter controlled_inverter_3
  assign OBS = or_51_out ? ~IR_0_7[3:2] : 2'bz;  // Controlled_Inverter controlled_inverter_4
  or or_58 (Decoded_3bit_SR1[2], decoder_8_out0, decoder_8_out1);
  or or_59 (or_59_out, and_133_out, and_108_out, and_134_out);
  assign FS2 = or_59_out ? 4'b0000 : 4'bz;  // Controlled_Buffer controlled_buffer_39
  or or_60 (or_60_out, and_109_out, and_110_out, and_111_out);
  assign FS2 = or_60_out ? 4'b0001 : 4'bz;  // Controlled_Buffer controlled_buffer_40
  or or_61 (or_61_out, and_112_out, and_113_out, and_114_out);
  assign FS2 = or_61_out ? 4'b0011 : 4'bz;  // Controlled_Buffer controlled_buffer_41
  or or_62 (or_62_out, and_115_out, and_116_out, and_117_out);
  assign FS2 = or_62_out ? 4'b0100 : 4'bz;  // Controlled_Buffer controlled_buffer_42
  or or_63 (or_63_out, and_118_out, and_119_out, and_120_out);
  assign FS2 = or_63_out ? 4'b0101 : 4'bz;  // Controlled_Buffer controlled_buffer_43
  assign OAS = or_56_out ? IR_0_7[6:5] : 2'bz;  // Controlled_Buffer controlled_buffer_44
  not not_1 (not_1_out, AM);
  // AND_Gate and_135 has open pins: in0=D5, in1=T0, out=open
  // AND_Gate and_136 has open pins: in0=D6, in1=T0, out=open
  and and_137 (and_137_out, D0, not_1_out, T5);
  and and_138 (and_138_out, D0, AM, T3);
  and and_139 (and_139_out, D1, T2);
  and and_140 (and_140_out, D2, T4);
  and and_141 (and_141_out, D3, T0);
  and and_142 (and_142_out, D4, T0);
  and and_143 (and_143_out, D7, T1);
  and and_144 (and_144_out, D8, T1);
  // AND_Gate and_145 has open pins: in0=D0, in1=T0, out=open
  // AND_Gate and_146 has open pins: in0=D0, in1=T0, out=open
  // AND_Gate and_147 has open pins: in0=D0, in1=T0, out=open
  // AND_Gate and_148 has open pins: in0=D0, in1=T0, out=open
  // AND_Gate and_149 has open pins: in0=D0, in1=T0, out=open
  // AND_Gate and_150 has open pins: in0=D0, in1=T0, out=open
  // AND_Gate and_151 has open pins: in0=D0, in1=T0, out=open
  // AND_Gate and_152 has open pins: in0=D0, in1=T0, out=open
  // AND_Gate and_153 has open pins: in0=D0, in1=T0, out=open
  or or_64 (CLEAR, and_137_out, and_138_out, and_139_out, and_140_out, and_141_out, and_142_out, and_143_out, and_144_out);

  // Other names for the same wires on the sheet: CLK = in_2; DR_L2[0] = AM; IR_8_15[2:0] = {DR_F1, DR_L2[1], AM};
  //   RS[1:0] = {DR_F1, DR_L2[1]}; SR2_F1 = IR_0_7[4]; SR1_L2[1:0] = IR_0_7[6:5]; SR1_F1 = IR_0_7[7];
  //   OPCODE[4:0] = IR_8_15; MAS_E = in_3; MBS_E = in_4; SR2_L2[1:0] = IR_0_7[3:2]

  // Notes on the sheet:
  //   MuxBSel
  //   FunSel3
  //   Load/Store
  //   Low/High
  //   FunSel4
  //   OutCSel
  //   RegSel1
  //   MuxASel
  //   RegSel3
  //   OutBSel
  //   FunSel2
  //   FunSel1
  //   OutASel
endmodule
