// Logisim project Project2Part2.circ as structural Verilog: 1 circuit, main circuit main
module main (
  input  [1:0] FunSel,
  input  [3:0] FunSel_2,
  input  clock,
  input  [3:0] RegSel,
  input  [1:0] OutASel,
  input  [1:0] OutBSel,
  input  [1:0] FunSel_3,
  input  in_8,
  input  [1:0] MuxASel,
  input  in_10,
  input  [2:0] RegSel_2,
  input  [1:0] MuxBSel,
  input  in_13,
  input  [1:0] OutCSel,
  input  Enable,
  input  [1:0] FunSel_4,
  input  L_H,
  output [7:0] IR_8_15
);

  wire not_1_out;
  wire [3:0] ALU_out_6;
  wire [7:0] ALU_output, main_1_outa, main_1_outb, main_2_output, main_3_outa, multiplexer_1_out,
       multiplexer_2_out, ram_1_data;

  _2a_main main_1 (
    .Load(multiplexer_1_out), .FunSel(FunSel), .RegSel(RegSel), .OutASel(OutASel), .OutBSel(OutBSel),
    .OutA(main_1_outa), .OutB(main_1_outb));  // open: clock, in_4, in_5, in_7
  Multiplexer #(.select(2), .width(8)) multiplexer_1 (
    .in0(ALU_output), .in1(main_3_outa), .in2(ram_1_data), .in3(main_2_output), .out(multiplexer_1_out),
    .sel(MuxASel), .en(in_8));
  _2c_main main_2 (
    .Enable(Enable), .clock(clock), .\input (ram_1_data), .Output({IR_8_15, main_2_output}), .L_H(L_H),
    .Funsel(FunSel_4));  // open: in_4
  Project2Part1_main ALU (
    .FunSel(FunSel_2), .cin(ALU_out_6[2]), .A(main_1_outa), .B(main_1_outb), .Output(ALU_output),
    .out_6(ALU_out_6));
  Multiplexer #(.select(2), .width(8)) multiplexer_2 (
    .in0(ALU_output), .in1(ram_1_data), .in2(ram_1_data), .in3(main_2_output), .out(multiplexer_2_out),
    .sel(MuxBSel), .en(in_10));
  Hex_Digit_Display hex_digit_display_1 (.value(IR_8_15[7:4]));  // open: dp
  Hex_Digit_Display hex_digit_display_2 (.value(IR_8_15[3:0]));  // open: dp
  _2b_main main_3 (
    .clock(clock), .Load(multiplexer_2_out), .FunSel(FunSel_3), .RegSel(RegSel_2), .OutCSel(OutCSel),
    .OutA(main_3_outa));  // open: in_4, in_5
  not not_1 (not_1_out, in_13);
  RAM #(.bus("separate")) ram_1 (
    .addr(main_3_outa), .din(ALU_output), .data(ram_1_data), .str(not_1_out), .clk(clock), .ld(in_13));  // open: sel, clr

  // Other names for the same wires on the sheet: cl = clock
endmodule
