// Logisim project Project2Part1.circ as structural Verilog: 1 circuit, main circuit main
module main (
  input  [3:0] FunSel,
  input  cin,
  input  [7:0] A,
  input  [7:0] B,
  output [7:0] Output,
  output [3:0] out_6
);

  wire and_2_out, and_3_out, and_4_out, and_5_out, and_6_out, and_7_out, and_8_out, c2, c3, c4, c13, c14,
       nand_1_out, nor_1_out, nor_2_out, or_2_out, or_3_out, undriven, xor_2_out, xor_3_out, xor_4_out,
       xor_5_out;
  wire [6:0] shifter_6_out;
  wire [7:0] _2, _3, _4, and_1_out, not_1_out, not_2_out, or_1_out, shifter_1_out, shifter_2_out,
       shifter_3_out, shifter_4_out, xor_1_out;
  wire [7:1] shifter_5_out;

  assign not_1_out = ~B;  // NOT_Gate not_1, 8 bits wide
  assign not_2_out = ~A;  // NOT_Gate not_2, 8 bits wide
  Adder adder_1 (.a(A), .b(B), .out(_3), .cin(cin), .cout(c3));
  Adder adder_2 (.a(A), .b(B), .out(_2), .cin(undriven), .cout(c2));
  Subtractor subtractor_1 (.a(A), .b(B), .out(_4), .bout(c4));  // open: bin
  assign and_1_out = A & B;  // AND_Gate and_1, 8 bits wide
  assign or_1_out = A | B;  // OR_Gate or_1, 8 bits wide
  assign xor_1_out = A ^ B;  // XOR_Gate xor_1, 8 bits wide
  Shifter shifter_1 (.in(A), .\dist (3'b001), .out(shifter_1_out));
  Shifter #(.shift("lr")) shifter_2 (.in(A), .\dist (3'b001), .out(shifter_2_out));
  Shifter shifter_3 (.in(A), .\dist (3'b001), .out(shifter_3_out));
  Shifter #(.shift("ar")) shifter_4 (.in(A), .\dist (3'b001), .out(shifter_4_out));
  Shifter #(.shift("rl")) shifter_5 (.in(A), .\dist (3'b001), .out({shifter_5_out, c13}));
  Shifter #(.shift("rr")) shifter_6 (.in(A), .\dist (3'b001), .out({c14, shifter_6_out}));
  Hex_Digit_Display hex_digit_display_1 (.value(A[7:4]));  // open: dp
  Hex_Digit_Display hex_digit_display_2 (.value(A[3:0]));  // open: dp
  and and_2 (and_2_out, A[7], B[7]);
  nor nor_1 (nor_1_out, A[7], B[7]);
  and and_3 (and_3_out, A[7], B[7]);
  nor nor_2 (nor_2_out, A[7], B[7]);
  xor xor_2 (xor_2_out, _4[7], A[7]);
  xor xor_3 (xor_3_out, A[7], B[7]);
  xor xor_4 (xor_4_out, A[7], A[6]);
  xor xor_5 (xor_5_out, A[7], cin);
  Hex_Digit_Display hex_digit_display_3 (.value(FunSel));  // open: dp
  and and_4 (and_4_out, ~_2[7], and_2_out);  // AND_Gate
  and and_5 (and_5_out, _2[7], nor_1_out);
  and and_6 (and_6_out, ~_3[7], and_3_out);  // AND_Gate
  and and_7 (and_7_out, _3[7], nor_2_out);
  and and_8 (and_8_out, xor_2_out, xor_3_out);
  Hex_Digit_Display hex_digit_display_4 (.value(B[7:4]));  // open: dp
  Hex_Digit_Display hex_digit_display_5 (.value(B[3:0]));  // open: dp
  or or_2 (or_2_out, and_4_out, and_5_out);
  or or_3 (or_3_out, and_6_out, and_7_out);
  Hex_Digit_Display hex_digit_display_6 (.value(Output[7:4]));  // open: dp
  Multiplexer #(.select(4), .width(8), .enable("false")) multiplexer_1 (
    .in0(A), .in1(_2), .in2(_3), .in3(_4), .in4(and_1_out), .in5(or_1_out), .in6(not_2_out), .in7(xor_1_out),
    .in8(shifter_1_out), .in9(shifter_2_out), .in10(shifter_3_out), .in11(shifter_4_out),
    .in12({shifter_5_out, cin}), .in13({cin, shifter_6_out}), .in14(B), .in15(not_1_out), .out(Output),
    .sel(FunSel));
  Hex_Digit_Display hex_digit_display_7 (.value(Output[3:0]));  // open: dp
  Multiplexer #(.select(4), .enable("false")) multiplexer_2 (
    .in0(1'b0), .in1(c2), .in2(c3), .in3(c4), .in4(1'b0), .in5(1'b0), .in6(1'b0), .in7(1'b0), .in8(A[7]),
    .in9(1'b0), .in10(1'b0), .in11(1'b0), .in12(c13), .in13(c14), .in14(1'b0), .in15(1'b0), .out(out_6[2]),
    .sel(FunSel));
  Multiplexer #(.select(4), .enable("false")) multiplexer_3 (
    .in0(1'b0), .in1(or_2_out), .in2(or_3_out), .in3(and_8_out), .in4(1'b0), .in5(1'b0), .in6(1'b0),
    .in7(1'b0), .in8(1'b0), .in9(1'b0), .in10(xor_4_out), .in11(1'b0), .in12(xor_4_out), .in13(xor_5_out),
    .in14(1'b0), .in15(1'b0), .out(out_6[0]), .sel(FunSel));
  Hex_Digit_Display hex_digit_display_8 (.value(out_6));  // open: dp
  nor nor_3 (out_6[3], Output[0], Output[1], Output[2], Output[3], Output[4], Output[5], Output[6], Output[7]);
  nand nand_1 (nand_1_out, FunSel[0], FunSel[1], ~FunSel[2], FunSel[3]);  // NAND_Gate
  and and_9 (out_6[1], nand_1_out, Output[7]);

  // Other names for the same wires on the sheet: c9 = A[7]; fs[3:0] = FunSel

  // Notes on the sheet:
  //   A
  //   funsel
  //   B
  //   =
  //   output
  //   flag
endmodule
