// Logisim project Project3.circ as structural Verilog: 1 circuit, main circuit main
module main (
  input  in_1
);

  wire Cl, CLEAR, L_S, T0, T1, T2, T3, T4, T5, T6, T7, T8, T9, T10, T11, T12, T13, T14, T15;
  wire [1:0] FS1, FS3, FS4, MAS, MBS, OAS, OBS, OCS;
  wire [2:0] RS3;
  wire [3:0] counter_1_q, FS2, RS1;
  wire [7:0] IR_0_7, IR_8_15;

  // Project2Part2_main main_1: pin names not known; wires that end beside it: FS1, FS2, Cl, RS1, OAS, OBS, MAS, RS3, MBS, L_S, OCS, FS3, FS4, IR_8_15, IR_0_7
  Decoder #(.select(4), .enable("false")) decoder_1 (
    .out0(T0), .out1(T1), .out2(T2), .out3(T3), .out4(T4), .out5(T5), .out6(T6), .out7(T7), .out8(T8),
    .out9(T9), .out10(T10), .out11(T11), .out12(T12), .out13(T13), .out14(T14), .out15(T15), .sel(counter_1_q));
  Counter #(.width(4), .max('hf)) counter_1 (.Q(counter_1_q), .clk(in_1), .clr(CLEAR));  // open: load, D, count, carry
  Decoder #(.select(4), .enable("false")) decoder_2 ();  // open: out0, out1, out2, out3, out4, out5, out6, out7, out8, out9, out10, out11, out12, out13, out14, out15, sel

  // Other names for the same wires on the sheet: CLK = in_1
endmodule
