// Logisim project 2c.circ as structural Verilog: 1 circuit, main circuit main
module main (
  input  Enable,
  input  clock,
  input  [7:0] \input ,
  input  in_4,
  input  L_H,
  input  [1:0] Funsel,
  output [15:0] Output
);

  wire and_1_out, and_2_out;
  wire [1:0] multiplexer_1_out, multiplexer_2_out;
  wire [7:0] multiplexer_3_out, multiplexer_4_out;
  wire [15:0] adder_1_out, multiplexer_5_out, subtractor_1_out;

  Hex_Digit_Display hex_digit_display_1 (.value(\input [7:4]), .dp(in_4));
  Hex_Digit_Display hex_digit_display_2 (.value(\input [3:0]), .dp(in_4));
  _1a_main main_1 (
    .clock(clock), .FunSel(2'b11), .Enable(Enable), .Load__I(multiplexer_5_out[7:0]), .out_7(Output[7:0]));  // open: in_2, in_6
  _1a_main main_2 (
    .clock(clock), .FunSel(2'b11), .Enable(Enable), .Load__I(multiplexer_5_out[15:8]), .out_7(Output[15:8]));  // open: in_2, in_6
  Hex_Digit_Display hex_digit_display_3 (.value(Output[11:8]), .dp(in_4));
  Hex_Digit_Display hex_digit_display_4 (.value(Output[15:12]), .dp(in_4));
  Hex_Digit_Display hex_digit_display_5 (.value(Output[3:0]), .dp(in_4));
  Hex_Digit_Display hex_digit_display_6 (.value(Output[7:4]), .dp(in_4));
  Adder #(.width(16)) adder_1 (.a(Output), .b(16'h1), .out(adder_1_out));  // open: cin, cout
  Subtractor #(.width(16)) subtractor_1 (.a(Output), .b(16'h1), .out(subtractor_1_out));  // open: bin, bout
  Multiplexer #(.width(2), .enable("false")) multiplexer_1 (
    .in0(2'b00), .in1(multiplexer_2_out), .out(multiplexer_1_out), .sel(and_2_out));
  Multiplexer #(.width(2), .enable("false")) multiplexer_2 (
    .in0(2'b01), .in1(2'b10), .out(multiplexer_2_out), .sel(and_1_out));
  and and_1 (and_1_out, L_H, and_2_out);
  and and_2 (and_2_out, Funsel[1], Funsel[0]);
  Multiplexer #(.width(8), .enable("false")) multiplexer_3 (
    .in0(Output[7:0]), .in1(\input ), .out(multiplexer_3_out), .sel(multiplexer_1_out[1]));
  Multiplexer #(.width(8), .enable("false")) multiplexer_4 (
    .in0(Output[15:8]), .in1(\input ), .out(multiplexer_4_out), .sel(multiplexer_1_out[0]));
  Multiplexer #(.select(2), .width(16), .enable("false")) multiplexer_5 (
    .in0({16{1'b0}}), .in1(adder_1_out), .in2(subtractor_1_out),
    .in3({multiplexer_4_out, multiplexer_3_out}), .out(multiplexer_5_out), .sel(Funsel));

  // Notes on the sheet:
  //   input
  //   output
endmodule
