// Logisim project 2a.circ as structural Verilog: 1 circuit, main circuit main
module main (
  input  clock,
  input  [7:0] Load,
  input  [1:0] FunSel,
  input  in_4,
  input  in_5,
  input  [1:0] OutASel,
  input  in_7,
  input  [3:0] RegSel,
  input  [1:0] OutBSel,
  output [7:0] OutA,
  output [7:0] OutB
);

  wire [7:0] R0_out_7, R1_out_7, R2_out_7, R3_out_7;

  Hex_Digit_Display hex_digit_display_1 (.value(Load[3:0]), .dp(in_5));
  Hex_Digit_Display hex_digit_display_2 (.value(Load[7:4]), .dp(in_5));
  Hex_Digit_Display hex_digit_display_3 (.value(RegSel), .dp(in_5));
  _1a_main R0 (
    .clock(clock), .FunSel(FunSel), .Enable(RegSel[3]), .Load__I(Load), .out_7(R0_out_7));  // open: in_2, in_6
  _1a_main R1 (
    .clock(clock), .FunSel(FunSel), .Enable(RegSel[2]), .Load__I(Load), .out_7(R1_out_7));  // open: in_2, in_6
  _1a_main R2 (
    .clock(clock), .FunSel(FunSel), .Enable(RegSel[1]), .Load__I(Load), .out_7(R2_out_7));  // open: in_2, in_6
  _1a_main R3 (
    .clock(clock), .FunSel(FunSel), .Enable(RegSel[0]), .Load__I(Load), .out_7(R3_out_7));  // open: in_2, in_6
  Multiplexer #(.select(2), .width(8), .enable("false")) multiplexer_1 (
    .in0(R0_out_7), .in1(R1_out_7), .in2(R2_out_7), .in3(R3_out_7), .out(OutA), .sel(OutASel));
  Multiplexer #(.select(2), .width(8), .enable("false")) multiplexer_2 (
    .in0(R0_out_7), .in1(R1_out_7), .in2(R2_out_7), .in3(R3_out_7), .out(OutB), .sel(OutBSel));
  Hex_Digit_Display hex_digit_display_4 (.value(OutA[7:4]), .dp(in_4));
  Hex_Digit_Display hex_digit_display_5 (.value(OutB[7:4]), .dp(in_7));
  Hex_Digit_Display hex_digit_display_6 (.value(OutA[3:0]), .dp(in_4));
  Hex_Digit_Display hex_digit_display_7 (.value(OutB[3:0]), .dp(in_7));
endmodule
